// Digital circuit 2.dig as structural Verilog
module _2 (
  input  I_0,
  input  T_1,
  input  EN,
  input  T_2,
  input  I_1,
  input  I_2,
  input  I_3,
  input  S_0,
  input  S_1,
  input  S_2,
  input  T_0,
  input  Adr_0,
  input  Adr_1,
  input  Adr_2,
  input  Adr_3,
  output O_0,
  output O_1,
  output O_2,
  output O_3
);

  wire Clock, demultiplexer_1_out_0, demultiplexer_1_out_1, demultiplexer_1_out_2, demultiplexer_1_out_3;
  wire [3:0] R_0, R_1, R_2, R_3;

  _74189 _74189_1 (
    .pin2(1'b0), .pin8(1'b0), .pin13(Adr_0), .pin14(Adr_0), .pin15(Adr_0), .pin16(1'b1));  // open: pin1, pin3, pin4, pin5, pin6, pin7, pin9, pin10, pin11, pin12
  Button button_1 (.out(Clock));
  Multiplexer #(.Selector_Bits(3), .Bits(4)) multiplexer_1 (
    .sel({S_2, S_1, S_0}), .in_0(R_0), .in_1(R_1), .in_2(R_2), .in_3(R_3), .in_4({I_3, I_2, I_1, I_0}),
    .in_5({I_3, I_2, I_1, I_0}), .in_6({I_3, I_2, I_1, I_0}), .in_7({I_3, I_2, I_1, I_0}),
    .out({O_3, O_2, O_1, O_0}));
  Demultiplexer #(.Selector_Bits(3)) demultiplexer_1 (
    .sel({T_2, T_1, T_0}), .in(EN), .out_0(demultiplexer_1_out_0), .out_1(demultiplexer_1_out_1),
    .out_2(demultiplexer_1_out_2), .out_3(demultiplexer_1_out_3));  // open: out_4, out_5, out_6, out_7
  Register register_1 (.In({O_3, O_2, O_1, O_0}), .Clk(Clock), .En(demultiplexer_1_out_0), .Out(R_0));
  Register register_2 (.In({O_3, O_2, O_1, O_0}), .Clk(Clock), .En(demultiplexer_1_out_1), .Out(R_1));
  Register register_3 (.In({O_3, O_2, O_1, O_0}), .Clk(Clock), .En(demultiplexer_1_out_2), .Out(R_2));
  Register register_4 (.In({O_3, O_2, O_1, O_0}), .Clk(Clock), .En(demultiplexer_1_out_3), .Out(R_3));

  // Other names for the same wires on the sheet: Bus[3:0] = {O_3, O_2, O_1, O_0}; DIN[3:0] = {I_3, I_2, I_1, I_0};
  //   Undef[3:0] = {I_3, I_2, I_1, I_0}; Source[2:0] = {S_2, S_1, S_0}; Sel[2:0] = {T_2, T_1, T_0}
endmodule
